// Logisim project fib2.circ as structural Verilog: 1 circuit, main circuit main
module main (
  input  [2:0] in_1,
  output [3:0] out_2
);

  wire clk, comparator_1_lt, counter_2_q, enable, not_2_out;
  wire [3:0] adder_1_out, bit_extender_1_out, counter_1_q, multiplexer_1_out, now, prev;

  Counter #(.width(4), .max('hf), .ongoal("stay")) counter_1 (
    .Q(counter_1_q), .clk(clk));  // open: load, D, count, carry, clr
  Clock clock_1 (.out(clk));
  assign bit_extender_1_out = {{1{1'b0}}, in_1};  // Bit_Extender bit_extender_1
  Comparator #(.width(4), .mode("unsigned")) comparator_1 (
    .a(bit_extender_1_out), .b(counter_1_q), .lt(comparator_1_lt));  // open: gt, eq
  not not_1 (enable, comparator_1_lt);
  Multiplexer #(.width(4), .enable("false")) multiplexer_1 (
    .in0(4'b0001), .in1(now), .out(multiplexer_1_out), .sel(counter_2_q));
  Counter #(.width(1), .max('h1), .ongoal("stay")) counter_2 (
    .Q(counter_2_q), .clk(clk));  // open: load, D, count, carry, clr
  Adder #(.width(4)) adder_1 (.a(prev), .b(now), .out(adder_1_out));  // open: cin, cout
  Register #(.width(4)) u_prev (.D(multiplexer_1_out), .en(enable), .Q(prev), .clk(clk));  // open: clr
  Register #(.width(4)) u_now (.D(adder_1_out), .en(enable), .Q(now), .clk(clk));  // open: clr
  Multiplexer #(.width(4), .enable("false")) multiplexer_2 (.in0(4'b0000), .in1(now), .out(out_2), .sel(not_2_out));
  not not_2 (not_2_out, enable);
endmodule
