// Logisim project fib3.circ as structural Verilog: 7 circuits, main circuit main
module main (
  input  [31:0] \input ,
  output [31:0] out_2
);

  wire \break , clk, init, n_low, not_1_out, not_2_out;
  wire [31:0] a11, a12, a21, a22, s11, s12, s21, s22, \初值阵_1_out_1 , \初值阵_1_out_2 , \初值阵_1_out_3 ,
       \初值阵_1_out_4 , \单位阵_1_out_1 , \单位阵_1_out_2 , \单位阵_1_out_3 , \单位阵_1_out_4 , \单位阵_2_out_1 ,
       \单位阵_2_out_2 , \单位阵_2_out_3 , \单位阵_2_out_4 , \矩阵mux_1_out_10 , \矩阵mux_1_out_11 , \矩阵mux_1_out_12 ,
       \矩阵mux_1_out_13 , \矩阵mux_2_out_10 , \矩阵mux_2_out_11 , \矩阵mux_2_out_12 , \矩阵mux_2_out_13 ,
       \矩阵mux_3_out_10 , \矩阵mux_3_out_11 , \矩阵mux_3_out_12 , \矩阵mux_3_out_13 , \矩阵乘法_1_out_9 ,
       \矩阵乘法_1_out_10 , \矩阵乘法_1_out_11 , \矩阵乘法_1_out_12 , \矩阵乘法_2_out_9 , \矩阵乘法_2_out_10 , \矩阵乘法_2_out_11 ,
       \矩阵乘法_2_out_12 ;

  Clock clock_1 (.out(clk));
  Counter #(.width(1), .max('h1), .ongoal("stay")) counter_1 (.Q(init), .clk(clk));  // open: load, D, count, carry, clr
  \循环控制  \u_循环控制_1  (.\input (\input ), .n_low(n_low), .\break (\break ));  // open: in_2
  \单位阵  \u_单位阵_1  (.out_1(\单位阵_1_out_1 ), .out_2(\单位阵_1_out_2 ), .out_3(\单位阵_1_out_3 ), .out_4(\单位阵_1_out_4 ));
  \矩阵MUX  \u_矩阵mux_1  (
    .a11(\单位阵_1_out_1 ), .a12(\单位阵_1_out_2 ), .a21(\单位阵_1_out_3 ), .a22(\单位阵_1_out_4 ), .b11(a11), .b12(a12),
    .b21(a21), .b22(a22), .in_6(n_low), .out_10(\矩阵mux_1_out_10 ), .out_11(\矩阵mux_1_out_11 ),
    .out_12(\矩阵mux_1_out_12 ), .out_13(\矩阵mux_1_out_13 ));
  \矩阵乘法  \u_矩阵乘法_1  (
    .a11(a11), .a12(a12), .a21(a21), .a22(a22), .b11(a11), .b12(a12), .b21(a21), .b22(a22),
    .out_9(\矩阵乘法_1_out_9 ), .out_10(\矩阵乘法_1_out_10 ), .out_11(\矩阵乘法_1_out_11 ), .out_12(\矩阵乘法_1_out_12 ));
  \矩阵乘法  \u_矩阵乘法_2  (
    .a11(s11), .a12(s12), .a21(s21), .a22(s22), .b11(\矩阵mux_1_out_10 ), .b12(\矩阵mux_1_out_11 ),
    .b21(\矩阵mux_1_out_12 ), .b22(\矩阵mux_1_out_13 ), .out_9(\矩阵乘法_2_out_9 ), .out_10(\矩阵乘法_2_out_10 ),
    .out_11(\矩阵乘法_2_out_11 ), .out_12(\矩阵乘法_2_out_12 ));
  \初值阵  \u_初值阵_1  (.out_1(\初值阵_1_out_1 ), .out_2(\初值阵_1_out_2 ), .out_3(\初值阵_1_out_3 ), .out_4(\初值阵_1_out_4 ));
  \单位阵  \u_单位阵_2  (.out_1(\单位阵_2_out_1 ), .out_2(\单位阵_2_out_2 ), .out_3(\单位阵_2_out_3 ), .out_4(\单位阵_2_out_4 ));
  \矩阵MUX  \u_矩阵mux_2  (
    .a11(\单位阵_2_out_1 ), .a12(\单位阵_2_out_2 ), .a21(\单位阵_2_out_3 ), .a22(\单位阵_2_out_4 ), .b11(\矩阵乘法_2_out_9 ),
    .b12(\矩阵乘法_2_out_10 ), .b21(\矩阵乘法_2_out_11 ), .b22(\矩阵乘法_2_out_12 ), .in_6(init),
    .out_10(\矩阵mux_2_out_10 ), .out_11(\矩阵mux_2_out_11 ), .out_12(\矩阵mux_2_out_12 ), .out_13(\矩阵mux_2_out_13 ));
  \矩阵MUX  \u_矩阵mux_3  (
    .a11(\初值阵_1_out_1 ), .a12(\初值阵_1_out_2 ), .a21(\初值阵_1_out_3 ), .a22(\初值阵_1_out_4 ), .b11(\矩阵乘法_1_out_9 ),
    .b12(\矩阵乘法_1_out_10 ), .b21(\矩阵乘法_1_out_11 ), .b22(\矩阵乘法_1_out_12 ), .in_6(init),
    .out_10(\矩阵mux_3_out_10 ), .out_11(\矩阵mux_3_out_11 ), .out_12(\矩阵mux_3_out_12 ), .out_13(\矩阵mux_3_out_13 ));
  \矩阵寄存器  a (
    .a11_in(\矩阵mux_3_out_10 ), .a12_in(\矩阵mux_3_out_11 ), .a21_in(\矩阵mux_3_out_12 ),
    .a22_in(\矩阵mux_3_out_13 ), .clk(clk), .out_7(a11), .out_8(a12), .out_9(a21), .out_10(a22), .ena(not_1_out));
  not not_1 (not_1_out, \break );
  \矩阵寄存器  s (
    .a11_in(\矩阵mux_2_out_10 ), .a12_in(\矩阵mux_2_out_11 ), .a21_in(\矩阵mux_2_out_12 ),
    .a22_in(\矩阵mux_2_out_13 ), .clk(clk), .out_7(s11), .out_8(s12), .out_9(s21), .out_10(s22), .ena(not_2_out));
  not not_2 (not_2_out, \break );
  Multiplexer #(.width(32), .enable("false")) multiplexer_1 (.in0({32{1'b0}}), .in1(s12), .out(out_2), .sel(\break ));
endmodule

module \循环控制  (
  input  [31:0] \input ,
  input  in_2,
  output n_low,
  output \break 
);

  wire clk, comparator_1_eq, init;
  wire [31:0] multiplexer_1_out, n, shifter_1_out;

  Counter #(.width(1), .max('h1), .ongoal("stay")) counter_1 (
    .Q(init), .clk(clk), .clr(in_2));  // open: load, D, count, carry
  Clock clock_1 (.out(clk));
  Shifter #(.width(32), .shift("lr")) shifter_1 (.in(n), .\dist (5'b00001), .out(shifter_1_out));
  Multiplexer #(.width(32), .enable("false")) multiplexer_1 (
    .in0(\input ), .in1(shifter_1_out), .out(multiplexer_1_out), .sel(init));
  Bit_Extender #(.in_width(32), .out_width(1)) bit_extender_1 (.in(n), .out(n_low));
  Comparator #(.width(32), .mode("unsigned")) comparator_1 (
    .a({32{1'b0}}), .b(n), .eq(comparator_1_eq));  // open: gt, lt
  Register #(.width(32)) register_1 (.D(multiplexer_1_out), .Q(n), .clk(clk), .clr(in_2));  // open: en
  Multiplexer #(.enable("false")) multiplexer_2 (.in0(1'b0), .in1(comparator_1_eq), .out(\break ), .sel(init));

  // Other names for the same wires on the sheet: clr = in_2
endmodule

module \矩阵乘法  (
  input  [31:0] a11,
  input  [31:0] a12,
  input  [31:0] a21,
  input  [31:0] a22,
  input  [31:0] b11,
  input  [31:0] b12,
  input  [31:0] b21,
  input  [31:0] b22,
  output [31:0] out_9,
  output [31:0] out_10,
  output [31:0] out_11,
  output [31:0] out_12
);

  wire [31:0] multiplier_1_out, multiplier_2_out, multiplier_3_out, multiplier_4_out, multiplier_5_out,
       multiplier_6_out, multiplier_7_out, multiplier_8_out;

  Multiplier #(.width(32)) multiplier_1 (.a(a11), .b(b11), .out(multiplier_1_out));  // open: cin, cout
  Multiplier #(.width(32)) multiplier_2 (.a(a12), .b(b21), .out(multiplier_2_out));  // open: cin, cout
  Multiplier #(.width(32)) multiplier_3 (.a(a11), .b(b12), .out(multiplier_3_out));  // open: cin, cout
  Multiplier #(.width(32)) multiplier_4 (.a(a12), .b(b22), .out(multiplier_4_out));  // open: cin, cout
  Multiplier #(.width(32)) multiplier_5 (.a(a21), .b(b11), .out(multiplier_5_out));  // open: cin, cout
  Multiplier #(.width(32)) multiplier_6 (.a(a22), .b(b21), .out(multiplier_6_out));  // open: cin, cout
  Multiplier #(.width(32)) multiplier_7 (.a(a21), .b(b12), .out(multiplier_7_out));  // open: cin, cout
  Multiplier #(.width(32)) multiplier_8 (.a(a22), .b(b22), .out(multiplier_8_out));  // open: cin, cout
  Adder #(.width(32)) adder_1 (.a(multiplier_1_out), .b(multiplier_2_out), .out(out_9));  // open: cin, cout
  Adder #(.width(32)) adder_2 (.a(multiplier_3_out), .b(multiplier_4_out), .out(out_10));  // open: cin, cout
  Adder #(.width(32)) adder_3 (.a(multiplier_5_out), .b(multiplier_6_out), .out(out_11));  // open: cin, cout
  Adder #(.width(32)) adder_4 (.a(multiplier_7_out), .b(multiplier_8_out), .out(out_12));  // open: cin, cout

  // Other names for the same wires on the sheet: c11[31:0] = out_9; c12[31:0] = out_10; c21[31:0] = out_11;
  //   c22[31:0] = out_12
endmodule

module \矩阵寄存器  (
  input  [31:0] a11_in,
  input  [31:0] a12_in,
  input  [31:0] a21_in,
  input  [31:0] a22_in,
  input  clk,
  input  ena,
  output [31:0] out_7,
  output [31:0] out_8,
  output [31:0] out_9,
  output [31:0] out_10
);

  Register #(.width(32)) register_1 (.D(a11_in), .en(ena), .Q(out_7), .clk(clk));  // open: clr
  Register #(.width(32)) register_2 (.D(a21_in), .en(ena), .Q(out_9), .clk(clk));  // open: clr
  Register #(.width(32)) register_3 (.D(a12_in), .en(ena), .Q(out_8), .clk(clk));  // open: clr
  Register #(.width(32)) register_4 (.D(a22_in), .en(ena), .Q(out_10), .clk(clk));  // open: clr

  // Other names for the same wires on the sheet: a11_out[31:0] = out_7; a12_out[31:0] = out_8; a21_out[31:0] = out_9;
  //   a22_out[31:0] = out_10
endmodule

module \矩阵MUX  (
  input  [31:0] a11,
  input  [31:0] a12,
  input  [31:0] a21,
  input  [31:0] a22,
  input  [31:0] b11,
  input  in_6,
  input  [31:0] b12,
  input  [31:0] b21,
  input  [31:0] b22,
  output [31:0] out_10,
  output [31:0] out_11,
  output [31:0] out_12,
  output [31:0] out_13
);

  Multiplexer #(.width(32), .enable("false")) multiplexer_1 (.in0(a11), .in1(b11), .out(out_10), .sel(in_6));
  Multiplexer #(.width(32), .enable("false")) multiplexer_2 (.in0(a12), .in1(b12), .out(out_11), .sel(in_6));
  Multiplexer #(.width(32), .enable("false")) multiplexer_3 (.in0(a21), .in1(b21), .out(out_12), .sel(in_6));
  Multiplexer #(.width(32), .enable("false")) multiplexer_4 (.in0(a22), .in1(b22), .out(out_13), .sel(in_6));

  // Other names for the same wires on the sheet: c11[31:0] = out_10; c12[31:0] = out_11; c21[31:0] = out_12;
  //   c22[31:0] = out_13; sel = in_6
endmodule

module \单位阵  (
  output [31:0] out_1,
  output [31:0] out_2,
  output [31:0] out_3,
  output [31:0] out_4
);


  assign out_1 = 32'h1;
  assign out_2 = {32{1'b0}};
  assign out_3 = {32{1'b0}};
  assign out_4 = 32'h1;
endmodule

module \初值阵  (
  output [31:0] out_1,
  output [31:0] out_2,
  output [31:0] out_3,
  output [31:0] out_4
);


  assign out_1 = 32'h1;
  assign out_2 = 32'h1;
  assign out_3 = 32'h1;
  assign out_4 = {32{1'b0}};
endmodule
