// Logisim project fibonacci.circ as structural Verilog: 1 circuit, main circuit main
module main (
  input  [2:0] in_1,
  output [3:0] out_2
);

  wire clock_1_out, comparator_1_gt, not_1_out;
  wire [2:0] counter_1_q;
  wire [3:0] adder_1_out, now_q, prev_q;

  Clock clock_1 (.out(clock_1_out));
  Counter #(.width(3), .max('h7), .ongoal("stay")) counter_1 (
    .Q(counter_1_q), .clk(clock_1_out));  // open: load, D, count, carry, clr
  Comparator #(.width(3), .mode("unsigned")) comparator_1 (
    .a(in_1), .b(counter_1_q), .gt(comparator_1_gt));  // open: eq, lt
  Adder #(.width(4)) adder_1 (.a(prev_q), .b(now_q), .out(adder_1_out));  // open: cin, cout
  Register #(.width(4)) prev (.D(now_q), .en(comparator_1_gt), .Q(prev_q), .clk(clock_1_out));  // open: clr
  not not_1 (not_1_out, comparator_1_gt);
  Register #(.width(4)) now (.D(adder_1_out), .en(comparator_1_gt), .Q(now_q), .clk(clock_1_out));  // open: clr
  Multiplexer #(.width(4), .enable("false")) multiplexer_1 (.in0(4'b0000), .in1(now_q), .out(out_2), .sel(not_1_out));
endmodule
