// Logisim project CRC.circ as structural Verilog: 3 circuits, main circuit main
module main (
  input  [7:0] A,
  input  [3:0] B,
  output [10:0] C
);

  wire [2:0] dd_1_p3, dd_2_p3, dd_3_p3, dd_4_p3, dd_6_p3, dd_7_p3;
  wire [3:1] dd_5_p3;

  // dd dd_1: pin names not known; wires that end beside it: {3'b000, A[7]}, B, dd_1_p3
  // dd dd_2: pin names not known; wires that end beside it: {dd_1_p3, A[6]}, B, dd_2_p3
  // dd dd_3: pin names not known; wires that end beside it: {dd_2_p3, A[5]}, B, dd_3_p3
  // dd dd_4: pin names not known; wires that end beside it: {dd_3_p3, A[4]}, B, dd_4_p3
  // dd dd_5: pin names not known; wires that end beside it: {dd_4_p3, A[3]}, B, dd_5_p3
  // dd dd_6: pin names not known; wires that end beside it: {dd_5_p3, A[2]}, B, dd_6_p3
  // dd dd_7: pin names not known; wires that end beside it: {dd_6_p3, A[1]}, B, dd_7_p3
  // dd dd_8: pin names not known; wires that end beside it: {dd_7_p3, A[0]}, B, C[2:0]

  assign C[10:3] = A;

  // Other names for the same wires on the sheet: div[3:0] = B
endmodule

module dd (
  input  [3:0] dividend,
  input  [3:0] divider,
  output [2:0] remain
);

  wire not_1_out;
  wire [3:0] multiplexer_1_out;
  wire [3:3] xor_1_out;

  not not_1 (not_1_out, dividend[3]);
  Multiplexer #(.width(4), .enable("false")) multiplexer_1 (
    .in0(divider), .in1(4'b0000), .out(multiplexer_1_out), .sel(not_1_out));
  assign {xor_1_out[3], remain} = dividend ^ multiplexer_1_out;  // XOR_Gate xor_1, 4 bits wide
endmodule

module CRC (
  input  [7:0] a,
  input  [3:0] b,
  output [10:0] c
);

  wire [2:0] dd_1_remain, dd_2_remain, dd_3_remain, dd_4_remain, dd_5_remain, dd_6_remain, dd_7_remain;

  Pull_Resistor pull_resistor_1 (.node(b));
  Pull_Resistor pull_resistor_2 (.node(a));
  dd dd_1 (.dividend(a[7:4]), .divider(b), .remain(dd_1_remain));
  dd dd_2 (.dividend({dd_1_remain, a[3]}), .divider(b), .remain(dd_2_remain));
  dd dd_3 (.dividend({dd_2_remain, a[2]}), .divider(b), .remain(dd_3_remain));
  dd dd_4 (.dividend({dd_3_remain, a[1]}), .divider(b), .remain(dd_4_remain));
  dd dd_5 (.dividend({dd_4_remain, a[0]}), .divider(b), .remain(dd_5_remain));
  dd dd_6 (.dividend({dd_5_remain, 1'b0}), .divider(b), .remain(dd_6_remain));
  dd dd_7 (.dividend({dd_6_remain, 1'b0}), .divider(b), .remain(dd_7_remain));
  dd dd_8 (.dividend({dd_7_remain, 1'b0}), .divider(b), .remain(c[2:0]));

  assign c[10:3] = a;
endmodule
