// Logisim project fsm.circ as structural Verilog: 4 circuits, main circuit main
module main (
  output out_1,
  output z,
  output out_3
);

  wire clock_1_out;
  wire [1:0] rom_1_data;
  wire [7:0] counter_1_q;

  Counter counter_1 (.Q(counter_1_q), .carry(out_3), .clk(clock_1_out));  // open: load, D, count, clr
  Clock clock_1 (.out(clock_1_out));
  ROM #(.dataWidth(3)) rom_1 (.addr(counter_1_q), .data({out_1, rom_1_data}));  // open: sel
  // Probe on rom_1_data
  fsm fsm_1 (.CLR(out_1), .in(rom_1_data), .z(z));

  // Notes on the sheet:
  //   contents of rom_1 (hex, n*v repeats v):
  //   1 0 0 2
endmodule

module fsm (
  input  CLR,
  input  [1:0] in,
  output z
);

  wire clk, clr_t;
  wire [1:0] comb_1_ns2, register_2_q;

  Register #(.width(1)) register_1 (.D(CLR), .Q(clr_t), .clk(clk), .clr(clr_t));  // open: en
  Clock clock_1 (.out(clk));
  comb comb_1 (
    .s1(register_2_q[1]), .s0(register_2_q[0]), .in1(in[1]), .in0(in[0]), .ns1(comb_1_ns2[1]),
    .ns2(comb_1_ns2[0]));
  Register #(.width(2)) register_2 (.D(comb_1_ns2), .Q(register_2_q), .clk(clk), .clr(clr_t));  // open: en
  out out_1 (.s1(register_2_q[1]), .s0(register_2_q[0]), .in1(in[1]), .in0(in[0]), .z(z));
endmodule

module comb (
  input  s1,
  input  s0,
  input  in1,
  input  in0,
  output ns1,
  output ns2
);

  wire and_1_out, and_2_out, and_3_out, and_4_out, and_5_out, and_6_out, and_7_out, not_1_out, not_2_out,
       not_3_out, not_4_out, not_5_out, not_6_out, not_7_out, not_8_out, not_9_out, not_10_out, not_11_out,
       not_12_out, not_13_out, not_14_out;

  not not_1 (not_1_out, s1);
  and and_1 (and_1_out, not_1_out, s0, not_2_out);
  not not_2 (not_2_out, in1);
  not not_3 (not_3_out, s1);
  and and_2 (and_2_out, not_3_out, s0, not_4_out);
  not not_4 (not_4_out, in0);
  and and_3 (and_3_out, s1, not_5_out, not_6_out);
  not not_5 (not_5_out, s0);
  not not_6 (not_6_out, in0);
  not not_7 (not_7_out, s1);
  not not_8 (not_8_out, s0);
  not not_9 (not_9_out, in1);
  not not_10 (not_10_out, s1);
  not not_11 (not_11_out, in0);
  not not_12 (not_12_out, s0);
  not not_13 (not_13_out, in0);
  not not_14 (not_14_out, in1);
  or or_1 (ns1, and_1_out, and_2_out, and_3_out);
  and and_4 (and_4_out, not_7_out, not_8_out, not_9_out, in0);
  and and_5 (and_5_out, not_10_out, s0, not_11_out);
  and and_6 (and_6_out, s1, not_12_out, not_13_out);
  and and_7 (and_7_out, s1, s0, not_14_out, in0);
  or or_2 (ns2, and_4_out, and_5_out, and_6_out, and_7_out);
endmodule

module out (
  input  s1,
  input  s0,
  input  in1,
  input  in0,
  output z
);

  wire not_1_out;

  and and_1 (z, s1, s0, not_1_out);
  not not_1 (not_1_out, in0);
endmodule
