// Logisim project ftoi.circ as structural Verilog
module ftoi (
  input  [15:0] float,
  output [31:0] out_2
);

  wire sel_1_sel;
  wire [4:0] adder_1_out;
  wire [10:0] bit_extender_1_out;
  wire [31:0] adder_2_out, ans, bit_extender_2_out, not_1_out, shifter_1_out, tmp;

  Adder #(.width(5)) adder_1 (.a(float[14:10]), .b(5'b10000), .out(adder_1_out), .cin(1'b1));  // open: cout
  assign not_1_out = ~tmp;  // NOT_Gate not_1, 32 bits wide
  assign bit_extender_1_out = {{1{1'b1}}, float[9:0]};  // Bit_Extender bit_extender_1
  assign bit_extender_2_out = {{21{1'b0}}, bit_extender_1_out};  // Bit_Extender bit_extender_2
  // Probe on adder_1_out
  Adder #(.width(32)) adder_2 (.a(not_1_out), .b(32'h1), .out(adder_2_out));  // open: cin, cout
  Shifter #(.width(32)) shifter_1 (.in(bit_extender_2_out), .\dist (adder_1_out), .out(shifter_1_out));
  Multiplexer #(.width(32), .enable("false")) multiplexer_1 (.in0(tmp), .in1(adder_2_out), .out(ans), .sel(float[15]));
  Shifter #(.width(32), .shift("lr")) shifter_2 (.in(shifter_1_out), .\dist (5'b01010), .out(tmp));
  SEL sel_1 (.in_1(float[14:10]), .sel(sel_1_sel));
  Multiplexer #(.width(32), .enable("false")) multiplexer_2 (.in0({32{1'b0}}), .in1(ans), .out(out_2), .sel(sel_1_sel));

  // Other names for the same wires on the sheet: M[9:0] = float[9:0]; E[4:0] = float[14:10]; S = float[15]
endmodule

module SEL (
  input  [4:0] in_1,
  output sel
);

  wire and_1_out, and_2_out, and_3_out, and_4_out, and_5_out, not_1_out, not_2_out, not_3_out, not_4_out,
       not_5_out;

  not not_1 (not_1_out, in_1[4]);
  and and_1 (and_1_out, not_1_out, in_1[3], in_1[2], in_1[1], in_1[0]);
  and and_2 (and_2_out, in_1[4], not_2_out);
  not not_2 (not_2_out, in_1[3]);
  and and_3 (and_3_out, in_1[4], not_3_out);
  not not_3 (not_3_out, in_1[2]);
  and and_4 (and_4_out, in_1[4], not_4_out);
  not not_4 (not_4_out, in_1[1]);
  and and_5 (and_5_out, in_1[4], not_5_out);
  not not_5 (not_5_out, in_1[0]);
  or or_1 (sel, and_1_out, and_2_out, and_3_out, and_4_out, and_5_out);
endmodule
