// Logisim project grf_new.circ as structural Verilog: 4 circuits, main circuit grf_8
module grf (
  input  clk,
  input  reset,
  input  WE,
  input  [4:0] A1,
  input  [4:0] A2,
  input  [4:0] A3,
  input  [31:0] WD,
  output [31:0] RD1,
  output [31:0] RD2
);

  wire [31:0] RD1_0, RD1_1, RD1_2, RD1_3, RD2_0, RD2_1, RD2_2, RD2_3, WD0, WD1, WD2, WD3;

  Demultiplexer #(.select(2), .width(32), .tristate("true")) demultiplexer_1 (
    .out0(WD0), .out1(WD1), .out2(WD2), .out3(WD3), .in(WD), .sel(A3[4:3]));  // open: en
  grf_80 _0 (
    .clk(clk), .clr(reset), .we(WE), .a1(A1[2:0]), .a2(A2[2:0]), .a3(A3[2:0]), .in_7(WD0), .out_8(RD1_0),
    .out_9(RD2_0));
  grf_8 _1 (
    .clr(reset), .we(WE), .a1(A1[2:0]), .a2(A2[2:0]), .a3(A3[2:0]), .in_7(WD1), .out_8(RD1_1), .out_9(RD2_1),
    .clk(clk));
  grf_8 _2 (
    .clr(reset), .we(WE), .a1(A1[2:0]), .a2(A2[2:0]), .a3(A3[2:0]), .in_7(WD2), .out_8(RD1_2), .out_9(RD2_2),
    .clk(clk));
  grf_8 _3 (
    .clr(reset), .we(WE), .a1(A1[2:0]), .a2(A2[2:0]), .a3(A3[2:0]), .in_7(WD3), .out_8(RD1_3), .out_9(RD2_3),
    .clk(clk));
  Multiplexer #(.select(2), .width(32)) multiplexer_1 (
    .in0(RD1_0), .in1(RD1_1), .in2(RD1_2), .in3(RD1_3), .out(RD1), .sel(A1[4:3]));  // open: en
  Multiplexer #(.select(2), .width(32)) multiplexer_2 (
    .in0(RD2_0), .in1(RD2_1), .in2(RD2_2), .in3(RD2_3), .out(RD2), .sel(A2[4:3]));  // open: en

  // Other names for the same wires on the sheet: A1_low[2:0] = A1[2:0]; A1_high[1:0] = A1[4:3]; A2_low[2:0] = A2[2:0];
  //   A2_high[1:0] = A2[4:3]; A3_low[2:0] = A3[2:0]; A3_high[1:0] = A3[4:3]; clr = reset
endmodule

module grf_8 (
  input  clk,
  input  clr,
  input  we,
  input  [2:0] a1,
  input  [2:0] a2,
  input  [2:0] a3,
  input  [31:0] in_7,
  output [31:0] out_8,
  output [31:0] out_9
);

  wire [31:0] i0, i1, i2, i3, i4, i5, i6, i7, o0, o1, o2, o3, o4, o5, o6, o7;

  Register #(.width(32)) register_1 (.D(i0), .Q(o0), .clk(clk), .clr(clr));  // open: en
  Multiplexer #(.select(3), .width(32)) multiplexer_1 (
    .in0(o0), .in1(o1), .in2(o2), .in3(o3), .in4(o4), .in5(o5), .in6(o6), .in7(o7), .out(out_8), .sel(a1));  // open: en
  Register #(.width(32)) register_2 (.D(i1), .Q(o1), .clk(clk), .clr(clr));  // open: en
  Register #(.width(32)) register_3 (.D(i2), .Q(o2), .clk(clk), .clr(clr));  // open: en
  Multiplexer #(.select(3), .width(32)) multiplexer_2 (
    .in0(o0), .in1(o1), .in2(o2), .in3(o3), .in4(o4), .in5(o5), .in6(o6), .in7(o7), .out(out_9), .sel(a2));  // open: en
  Register #(.width(32)) register_4 (.D(i3), .Q(o3), .clk(clk), .clr(clr));  // open: en
  Register #(.width(32)) register_5 (.D(i4), .Q(o4), .clk(clk), .clr(clr));  // open: en
  Demultiplexer #(.select(3), .width(32), .tristate("true")) demultiplexer_1 (
    .out0(i0), .out1(i1), .out2(i2), .out3(i3), .out4(i4), .out5(i5), .out6(i6), .out7(i7), .in(in_7),
    .sel(a3), .en(we));
  Register #(.width(32)) register_6 (.D(i5), .Q(o5), .clk(clk), .clr(clr));  // open: en
  Register #(.width(32)) register_7 (.D(i6), .Q(o6), .clk(clk), .clr(clr));  // open: en
  Register #(.width(32)) register_8 (.D(i7), .Q(o7), .clk(clk), .clr(clr));  // open: en

  // Other names for the same wires on the sheet: rd1[31:0] = out_8; rd2[31:0] = out_9; wd[31:0] = in_7
endmodule

module grf_80 (
  input  clk,
  input  clr,
  input  we,
  input  [2:0] a1,
  input  [2:0] a2,
  input  [2:0] a3,
  input  [31:0] in_7,
  output [31:0] out_8,
  output [31:0] out_9
);

  wire [31:0] i0, i1, i2, i3, i4, i5, i6, i7, o1, o2, o3, o4, o5, o6, o7;

  Multiplexer #(.select(3), .width(32)) multiplexer_1 (
    .in0({32{1'b0}}), .in1(o1), .in2(o2), .in3(o3), .in4(o4), .in5(o5), .in6(o6), .in7(o7), .out(out_8),
    .sel(a1));  // open: en
  Register #(.width(32)) register_1 (.D(i1), .Q(o1), .clk(clk), .clr(clr));  // open: en
  Register #(.width(32)) register_2 (.D(i2), .Q(o2), .clk(clk), .clr(clr));  // open: en
  Multiplexer #(.select(3), .width(32)) multiplexer_2 (
    .in0({32{1'b0}}), .in1(o1), .in2(o2), .in3(o3), .in4(o4), .in5(o5), .in6(o6), .in7(o7), .out(out_9),
    .sel(a2));  // open: en
  Register #(.width(32)) register_3 (.D(i3), .Q(o3), .clk(clk), .clr(clr));  // open: en
  Register #(.width(32)) register_4 (.D(i4), .Q(o4), .clk(clk), .clr(clr));  // open: en
  Demultiplexer #(.select(3), .width(32), .tristate("true")) demultiplexer_1 (
    .out0(i0), .out1(i1), .out2(i2), .out3(i3), .out4(i4), .out5(i5), .out6(i6), .out7(i7), .in(in_7),
    .sel(a3), .en(we));
  Register #(.width(32)) register_5 (.D(i5), .Q(o5), .clk(clk), .clr(clr));  // open: en
  Register #(.width(32)) register_6 (.D(i6), .Q(o6), .clk(clk), .clr(clr));  // open: en
  Register #(.width(32)) register_7 (.D(i7), .Q(o7), .clk(clk), .clr(clr));  // open: en

  // Other names for the same wires on the sheet: rd1[31:0] = out_8; rd2[31:0] = out_9; wd[31:0] = in_7
endmodule

module main (
  input  reset,
  output [31:0] RD1,
  output [31:0] RD2
);

  wire clk, WE;
  wire [4:0] A1, A2, A3;
  wire [7:0] add;
  wire [31:0] WD;

  Clock clock_1 (.out(clk));
  Counter counter_1 (.Q(add), .clk(clk));  // open: load, D, count, carry, clr
  ROM #(.dataWidth(1)) rom_1 (.addr(add), .data(WE));  // open: sel
  ROM #(.dataWidth(5)) rom_2 (.addr(add), .data(A1));  // open: sel
  ROM #(.dataWidth(5)) rom_3 (.addr(add), .data(A2));  // open: sel
  ROM #(.dataWidth(5)) rom_4 (.addr(add), .data(A3));  // open: sel
  ROM #(.dataWidth(32)) rom_5 (.addr(add), .data(WD));  // open: sel
  grf grf_1 (.reset(reset), .WE(WE), .A1(A1), .A2(A2), .A3(A3), .WD(WD), .RD1(RD1), .RD2(RD2), .clk(clk));
endmodule
