// Logisim project navigation.circ as structural Verilog
module navigation (
  input  [1:0] dir,
  input  clk,
  input  reset,
  output arrive,
  output hit
);

  wire comparator_1_eq, inital;
  wire [2:0] ns, pre_s, s;

  Counter #(.width(1), .max('h1), .ongoal("stay")) counter_1 (
    .Q(inital), .clk(clk), .clr(reset));  // open: load, D, count, carry
  // Probe on s
  comb2 comb2_1 (.s(s), .dir(dir), .ns(ns));
  Register #(.width(3)) register_1 (.D(s), .Q(pre_s), .clk(clk), .clr(reset));  // open: en
  Register #(.width(3)) register_2 (.D(ns), .Q(s), .clk(clk), .clr(reset));  // open: en
  Comparator #(.width(3), .mode("unsigned")) comparator_1 (.a(pre_s), .b(s), .eq(comparator_1_eq));  // open: gt, lt
  Multiplexer #(.enable("false")) multiplexer_1 (.in0(1'b0), .in1(comparator_1_eq), .out(hit), .sel(inital));
  arrive arrive_1 (.s(s), .arrive(arrive));
endmodule

module comb (
  input  [2:0] s,
  input  [1:0] dir,
  output [2:0] ns
);

  wire and_1_out, and_2_out, and_3_out, and_4_out, and_5_out, and_6_out, and_7_out, and_8_out, and_9_out,
       and_10_out, and_11_out, and_12_out, and_13_out, not_1_out, not_2_out, not_3_out, not_4_out, not_5_out,
       not_6_out, not_7_out, not_8_out, not_9_out, not_10_out, not_11_out, not_12_out, not_13_out,
       not_14_out, not_15_out, not_16_out, not_17_out, not_18_out, not_19_out, not_20_out, not_21_out,
       not_22_out;

  not not_1 (not_1_out, s[0]);
  not not_2 (not_2_out, dir[1]);
  not not_3 (not_3_out, dir[0]);
  not not_4 (not_4_out, dir[1]);
  not not_5 (not_5_out, s[0]);
  not not_6 (not_6_out, s[2]);
  not not_7 (not_7_out, s[1]);
  not not_8 (not_8_out, dir[1]);
  not not_9 (not_9_out, s[2]);
  not not_10 (not_10_out, dir[1]);
  not not_11 (not_11_out, dir[0]);
  not not_12 (not_12_out, s[0]);
  not not_13 (not_13_out, dir[1]);
  not not_14 (not_14_out, s[0]);
  not not_15 (not_15_out, dir[0]);
  not not_16 (not_16_out, s[2]);
  not not_17 (not_17_out, s[1]);
  not not_18 (not_18_out, dir[1]);
  not not_19 (not_19_out, dir[0]);
  not not_20 (not_20_out, s[2]);
  not not_21 (not_21_out, dir[0]);
  not not_22 (not_22_out, s[0]);
  and and_1 (and_1_out, s[1], not_1_out, not_2_out, not_3_out);
  and and_2 (and_2_out, s[1], s[0], not_4_out, dir[0]);
  and and_3 (and_3_out, s[2], not_5_out);
  and and_4 (and_4_out, not_6_out, not_7_out, s[0], not_8_out);
  and and_5 (and_5_out, not_9_out, s[0], not_10_out, not_11_out);
  and and_6 (and_6_out, s[1], not_12_out, not_13_out, dir[0]);
  and and_7 (and_7_out, s[1], not_14_out, dir[1], not_15_out);
  and and_8 (and_8_out, s[1], s[0], dir[1], dir[0]);
  and and_9 (and_9_out, not_16_out, not_17_out, not_18_out, not_19_out);
  and and_10 (and_10_out, not_20_out, s[0], dir[1], dir[0]);
  and and_11 (and_11_out, s[1], dir[1], dir[0]);
  and and_12 (and_12_out, s[1], s[0], not_21_out);
  and and_13 (and_13_out, s[2], not_22_out);
  or or_1 (ns[2], and_1_out, and_2_out, and_3_out);
  or or_2 (ns[1], and_4_out, and_5_out, and_6_out, and_7_out, and_8_out);
  or or_3 (ns[0], and_9_out, and_10_out, and_11_out, and_12_out, and_13_out);
endmodule

module arrive (
  input  [2:0] s,
  output arrive
);

  wire not_1_out;

  not not_1 (not_1_out, s[0]);
  and and_1 (arrive, s[2], not_1_out);
endmodule

module hit (
  input  [2:0] s,
  input  [1:0] dir,
  output hit
);

  wire and_1_out, and_2_out, and_3_out, and_4_out, and_5_out, not_1_out, not_2_out, not_3_out, not_4_out,
       not_5_out, not_6_out, not_7_out, not_8_out, not_9_out, not_10_out, not_11_out, not_12_out;

  not not_1 (not_1_out, s[2]);
  not not_2 (not_2_out, s[0]);
  not not_3 (not_3_out, dir[1]);
  not not_4 (not_4_out, s[2]);
  not not_5 (not_5_out, s[1]);
  not not_6 (not_6_out, s[0]);
  not not_7 (not_7_out, s[2]);
  not not_8 (not_8_out, s[0]);
  not not_9 (not_9_out, dir[0]);
  not not_10 (not_10_out, s[2]);
  not not_11 (not_11_out, dir[1]);
  not not_12 (not_12_out, dir[0]);
  and and_1 (and_1_out, not_1_out, not_2_out, not_3_out, dir[0]);
  and and_2 (and_2_out, not_4_out, not_5_out, not_6_out, dir[1]);
  and and_3 (and_3_out, not_7_out, not_8_out, dir[1], not_9_out);
  and and_4 (and_4_out, not_10_out, s[0], dir[1], dir[0]);
  and and_5 (and_5_out, s[1], s[0], not_11_out, not_12_out);
  or or_1 (hit, and_1_out, and_2_out, and_3_out, and_4_out, and_5_out);
endmodule

module hit2 (
  input  [2:0] s,
  input  [1:0] dir,
  output hit
);

  wire and_1_out, and_2_out, and_3_out, and_4_out, and_5_out, and_6_out, not_1_out, not_2_out, not_3_out,
       not_4_out, not_5_out, not_6_out, not_7_out, not_8_out, not_9_out, not_10_out, not_11_out;

  not not_1 (not_1_out, s[2]);
  not not_2 (not_2_out, s[0]);
  not not_3 (not_3_out, dir[1]);
  not not_4 (not_4_out, s[2]);
  not not_5 (not_5_out, s[1]);
  not not_6 (not_6_out, s[0]);
  not not_7 (not_7_out, s[2]);
  not not_8 (not_8_out, s[0]);
  not not_9 (not_9_out, dir[0]);
  not not_10 (not_10_out, dir[1]);
  not not_11 (not_11_out, dir[0]);
  and and_1 (and_1_out, not_1_out, not_2_out, not_3_out, dir[0]);
  and and_2 (and_2_out, not_4_out, not_5_out, not_6_out, dir[1]);
  and and_3 (and_3_out, not_7_out, not_8_out, dir[1], not_9_out);
  and and_4 (and_4_out, s[0], dir[1], dir[0]);
  and and_5 (and_5_out, s[1], s[0], not_10_out, not_11_out);
  and and_6 (and_6_out, s[2], s[0]);
  or or_1 (hit, and_1_out, and_2_out, and_3_out, and_4_out, and_5_out, and_6_out);
endmodule

module comb2 (
  input  [2:0] s,
  input  [1:0] dir,
  output [2:0] ns
);

  wire and_1_out, and_2_out, and_3_out, and_4_out, and_5_out, and_6_out, and_7_out, and_8_out, and_9_out,
       and_10_out, and_11_out, not_1_out, not_2_out, not_3_out, not_4_out, not_5_out, not_6_out, not_7_out,
       not_8_out, not_9_out, not_10_out, not_11_out, not_12_out, not_13_out, not_14_out, not_15_out,
       not_16_out, not_17_out;

  not not_1 (not_1_out, s[0]);
  not not_2 (not_2_out, dir[1]);
  not not_3 (not_3_out, dir[0]);
  not not_4 (not_4_out, dir[1]);
  not not_5 (not_5_out, s[1]);
  not not_6 (not_6_out, dir[1]);
  not not_7 (not_7_out, dir[1]);
  not not_8 (not_8_out, dir[0]);
  not not_9 (not_9_out, s[0]);
  not not_10 (not_10_out, dir[1]);
  not not_11 (not_11_out, s[0]);
  not not_12 (not_12_out, dir[0]);
  not not_13 (not_13_out, s[2]);
  not not_14 (not_14_out, s[1]);
  not not_15 (not_15_out, dir[1]);
  not not_16 (not_16_out, dir[0]);
  not not_17 (not_17_out, dir[0]);
  and and_1 (and_1_out, s[1], not_1_out, not_2_out, not_3_out);
  and and_2 (and_2_out, s[1], s[0], not_4_out, dir[0]);
  and and_3 (and_3_out, not_5_out, s[0], not_6_out);
  and and_4 (and_4_out, s[0], not_7_out, not_8_out);
  and and_5 (and_5_out, s[1], not_9_out, not_10_out, dir[0]);
  and and_6 (and_6_out, s[1], not_11_out, dir[1], not_12_out);
  and and_7 (and_7_out, s[1], s[0], dir[1], dir[0]);
  and and_8 (and_8_out, not_13_out, not_14_out, not_15_out, not_16_out);
  and and_9 (and_9_out, s[0], dir[1], dir[0]);
  and and_10 (and_10_out, s[1], dir[1], dir[0]);
  and and_11 (and_11_out, s[1], s[0], not_17_out);
  or or_1 (ns[2], and_1_out, and_2_out);
  or or_2 (ns[1], and_3_out, and_4_out, and_5_out, and_6_out, and_7_out);
  or or_3 (ns[0], and_8_out, and_9_out, and_10_out, and_11_out);
endmodule
