// Logisim project P3.circ as structural Verilog: 22 circuits, main circuit main
module main (
  input  clr,
  output [31:0] instr,
  output RegWrite,
  output [4:0] RegAddr,
  output [31:0] RegData,
  output MemWrite,
  output [4:0] MemAddr,
  output [31:0] MemData
);

  wire addu, and_1_out, beq, clk, equal, greater, \initial , j, jal, jr, less, lh, lui, lw, MemSrc, ori, sb,
       subu, sw;
  wire [1:0] ALUSrc, PCSrc, RegAddr3Src, RegSrc;
  wire [2:0] ALUOp;
  wire [4:0] InstrAdd, R1, R2, R3;
  wire [5:0] func, opcode;
  wire [15:0] offset;
  wire [25:0] index;
  wire [27:0] PC;
  wire [31:0] adder_2_out, ALUResult, branchAdd, lmask_1_ans, MemDataOut, multiplexer_1_out, nextPC, PC_4,
       RegDataOut1, RegDataOut2, shifter_1_out, SignImm, smask_1_ans, SrcB, subtractor_1_out, UnsignImm;
  wire [31:28] jIndex;

  // Probe on MemDataOut
  // Probe on RegWrite
  // Probe on MemWrite
  // Probe on RegSrc
  // Probe on ALUSrc
  // Probe on RegAddr3Src
  // Probe on PCSrc
  // Probe on MemSrc
  // Probe on ALUOp
  // Probe on offset
  // Probe on R1
  // Probe on R2
  // Probe on R3
  // Probe on opcode
  // Probe on ALUOp
  Clock u_clk (.out(clk));
  Register #(.width(32)) u_PC (.D(nextPC), .Q({jIndex, PC}), .clk(clk), .clr(clr));  // open: en
  CONTROLfront controlfront_1 (
    .opcode(opcode), .func(func), .lw(lw), .sw(sw), .addu(addu), .subu(subu), .ori(ori), .beq(beq),
    .lui(lui), .j(j), .jal(jal), .jr(jr), .sb(sb), .lh(lh));
  ROM #(.addrWidth(5), .dataWidth(32)) rom_1 (.addr(InstrAdd), .data(instr));  // open: sel
  ANALSIS analsis_1 (
    .offset(offset), .R2(R2), .R1(R1), .opcode(opcode), .in_1(instr), .SignImm(SignImm), .func(func),
    .R3(R3), .UnsignImm(UnsignImm), .index(index));
  GRF grf_1 (
    .clk(clk), .clr(clr), .we(RegWrite), .a1(R1), .a2(R2), .a3(RegAddr), .WD(RegData), .RD1(RegDataOut1),
    .RD2(RegDataOut2));
  ALU alu_1 (
    .srcA(RegDataOut1), .srcB(SrcB), .ALUControl(ALUOp),
    .ALUResult({ALUResult[31:7], MemAddr, ALUResult[1:0]}), .equal(equal), .greater(greater), .less(less));
  RAM #(.addrWidth(5), .dataWidth(32), .bus("separate")) ram_1 (
    .addr(MemAddr), .din(MemData), .data(MemDataOut), .str(MemWrite), .clk(clk), .ld(1'b1), .clr(clr));  // open: sel
  Multiplexer #(.width(32), .enable("false")) multiplexer_1 (
    .in0(32'h3000), .in1({jIndex, PC}), .out(multiplexer_1_out), .sel(\initial ));
  Counter #(.width(1), .max('h1), .ongoal("stay")) counter_1 (
    .Q(\initial ), .clk(clk), .clr(clr));  // open: load, D, count, carry
  Adder #(.width(32)) adder_1 (.a(multiplexer_1_out), .b(32'h4), .out(PC_4));  // open: cin, cout
  Subtractor #(.width(32)) subtractor_1 (
    .a({jIndex, PC}), .b(32'h3000), .out({subtractor_1_out[31:7], InstrAdd, subtractor_1_out[1:0]}));  // open: bin, bout
  CONTROLback controlback_1 (
    .lw(lw), .MemSrc(MemSrc), .MemWrite(MemWrite), .ALUOp(ALUOp), .sw(sw), .addu(addu), .subu(subu),
    .ori(ori), .beq(beq), .lui(lui), .ALUSrc(ALUSrc), .RegSrc(RegSrc), .jal(jal), .RegAddr3Src(RegAddr3Src),
    .sb(sb), .lh(lh), .RegWrite(RegWrite));
  Multiplexer #(.select(2), .width(32), .enable("false")) multiplexer_2 (
    .in0(PC_4), .in1(branchAdd), .in2({jIndex, index, 2'b00}), .in3(RegDataOut1), .out(nextPC), .sel(PCSrc));
  Multiplexer #(.select(2), .width(32), .enable("false")) multiplexer_3 (
    .in0(SignImm), .in1(RegDataOut2), .in2(UnsignImm), .out(SrcB), .sel(ALUSrc));  // open: in3
  and and_1 (and_1_out, equal, beq);
  or or_1 (PCSrc[0], and_1_out, jr);
  or or_2 (PCSrc[1], j, jr, jal);
  Multiplexer #(.select(2), .width(5), .enable("false")) multiplexer_4 (
    .in0(R2), .in1(R3), .in2({5{1'b1}}), .out(RegAddr), .sel(RegAddr3Src));  // open: in3
  Pull_Resistor pull_resistor_1 (.node(PCSrc));
  // Probe on RegDataOut2
  smask smask_1 (.R2(RegDataOut2), .MemAdd({ALUResult[31:7], MemAddr, ALUResult[1:0]}), .ans(smask_1_ans));
  Multiplexer #(.width(32), .enable("false")) multiplexer_5 (
    .in0(RegDataOut2), .in1(smask_1_ans), .out(MemData), .sel(MemSrc));
  // Probe on smask_1_ans
  Shifter #(.width(32)) shifter_1 (.in(SignImm), .\dist (5'b00010), .out(shifter_1_out));
  Adder #(.width(32)) adder_2 (.a(shifter_1_out), .b({jIndex, PC}), .out(adder_2_out));  // open: cin, cout
  Adder #(.width(32)) adder_3 (.a(adder_2_out), .b(32'h4), .out(branchAdd));  // open: cin, cout
  lmask lmask_1 (.MemDataOut(MemDataOut), .MemAdd({ALUResult[31:7], MemAddr, ALUResult[1:0]}), .ans(lmask_1_ans));
  Multiplexer #(.select(2), .width(32), .enable("false")) multiplexer_6 (
    .in0(MemDataOut), .in1({ALUResult[31:7], MemAddr, ALUResult[1:0]}), .in2(PC_4), .in3(lmask_1_ans),
    .out(RegData), .sel(RegSrc));

  // Other names for the same wires on the sheet: ALUResult[6:2] = MemAddr; MemAdd[4:0] = MemAddr;
  //   jIndex[27:2] = index; PC[31:28] = jIndex; MemDataIn[31:0] = MemData; RegAddr1[4:0] = R1; RegAddr2[4:0] = R2;
  //   RegAddr3[4:0] = RegAddr; RegDataIn[31:0] = RegData; SrcA[31:0] = RegDataOut1

  // Notes on the sheet:
  //   contents of rom_1 (hex, n*v repeats v):
  //   3c080064
endmodule

module ANALSIS (
  input  [31:0] in_1,
  output [15:0] offset,
  output [4:0] R2,
  output [4:0] R1,
  output [5:0] opcode,
  output [31:0] SignImm,
  output [5:0] func,
  output [4:0] R3,
  output [31:0] UnsignImm,
  output [25:0] index
);

  assign SignImm = {{16{in_1[15]}}, in_1[15:0]};  // Bit_Extender bit_extender_1
  assign UnsignImm = {{16{1'b0}}, in_1[15:0]};  // Bit_Extender bit_extender_2

  assign func = in_1[5:0];
  assign index = in_1[25:0];
  assign offset = in_1[15:0];
  assign opcode = in_1[31:26];
  assign R1 = in_1[25:21];
  assign R2 = in_1[20:16];
  assign R3 = in_1[15:11];

  // Other names for the same wires on the sheet: instr[31:0] = in_1
endmodule

module GRF (
  input  [31:0] WD,
  input  clk,
  input  clr,
  input  we,
  input  [4:0] a1,
  input  [4:0] a2,
  input  [4:0] a3,
  output [31:0] RD1,
  output [31:0] RD2
);

  wire [31:0] i0, i1, i2, i3, i4, i5, i6, i7, i8, i9, i10, i11, i12, i13, i14, i15, i16, i17, i18, i19, i20,
       i21, i22, i23, i24, i25, i26, i27, i28, i29, i30, i31, o1, o2, o3, o4, o5, o6, o7, o8, o9, o10, o11,
       o12, o13, o14, o15, o16, o17, o18, o19, o20, o21, o22, o23, o24, o25, o26, o27, o28, o29, o30, o31;

  Register #(.width(32)) register_1 (.D(i8), .Q(o8), .clk(clk), .clr(clr));  // open: en
  Register #(.width(32)) register_2 (.D(i16), .Q(o16), .clk(clk), .clr(clr));  // open: en
  Register #(.width(32)) register_3 (.D(i24), .Q(o24), .clk(clk), .clr(clr));  // open: en
  Register #(.width(32)) register_4 (.D(i1), .Q(o1), .clk(clk), .clr(clr));  // open: en
  Register #(.width(32)) register_5 (.D(i9), .Q(o9), .clk(clk), .clr(clr));  // open: en
  Register #(.width(32)) register_6 (.D(i17), .Q(o17), .clk(clk), .clr(clr));  // open: en
  Register #(.width(32)) register_7 (.D(i25), .Q(o25), .clk(clk), .clr(clr));  // open: en
  Register #(.width(32)) register_8 (.D(i2), .Q(o2), .clk(clk), .clr(clr));  // open: en
  Register #(.width(32)) register_9 (.D(i10), .Q(o10), .clk(clk), .clr(clr));  // open: en
  Register #(.width(32)) register_10 (.D(i18), .Q(o18), .clk(clk), .clr(clr));  // open: en
  Register #(.width(32)) register_11 (.D(i26), .Q(o26), .clk(clk), .clr(clr));  // open: en
  Register #(.width(32)) register_12 (.D(i3), .Q(o3), .clk(clk), .clr(clr));  // open: en
  Register #(.width(32)) register_13 (.D(i11), .Q(o11), .clk(clk), .clr(clr));  // open: en
  Register #(.width(32)) register_14 (.D(i19), .Q(o19), .clk(clk), .clr(clr));  // open: en
  Register #(.width(32)) register_15 (.D(i27), .Q(o27), .clk(clk), .clr(clr));  // open: en
  Demultiplexer #(.select(5), .width(32), .tristate("true")) demultiplexer_1 (
    .out0(i0), .out1(i1), .out2(i2), .out3(i3), .out4(i4), .out5(i5), .out6(i6), .out7(i7), .out8(i8),
    .out9(i9), .out10(i10), .out11(i11), .out12(i12), .out13(i13), .out14(i14), .out15(i15), .out16(i16),
    .out17(i17), .out18(i18), .out19(i19), .out20(i20), .out21(i21), .out22(i22), .out23(i23), .out24(i24),
    .out25(i25), .out26(i26), .out27(i27), .out28(i28), .out29(i29), .out30(i30), .out31(i31), .in(WD),
    .sel(a3), .en(we));
  Register #(.width(32)) register_16 (.D(i4), .Q(o4), .clk(clk), .clr(clr));  // open: en
  Register #(.width(32)) register_17 (.D(i12), .Q(o12), .clk(clk), .clr(clr));  // open: en
  Register #(.width(32)) register_18 (.D(i20), .Q(o20), .clk(clk), .clr(clr));  // open: en
  Register #(.width(32)) register_19 (.D(i28), .Q(o28), .clk(clk), .clr(clr));  // open: en
  Register #(.width(32)) register_20 (.D(i5), .Q(o5), .clk(clk), .clr(clr));  // open: en
  Register #(.width(32)) register_21 (.D(i13), .Q(o13), .clk(clk), .clr(clr));  // open: en
  Register #(.width(32)) register_22 (.D(i21), .Q(o21), .clk(clk), .clr(clr));  // open: en
  Register #(.width(32)) register_23 (.D(i29), .Q(o29), .clk(clk), .clr(clr));  // open: en
  Register #(.width(32)) register_24 (.D(i6), .Q(o6), .clk(clk), .clr(clr));  // open: en
  Register #(.width(32)) register_25 (.D(i14), .Q(o14), .clk(clk), .clr(clr));  // open: en
  Register #(.width(32)) register_26 (.D(i22), .Q(o22), .clk(clk), .clr(clr));  // open: en
  Register #(.width(32)) register_27 (.D(i30), .Q(o30), .clk(clk), .clr(clr));  // open: en
  Register #(.width(32)) register_28 (.D(i7), .Q(o7), .clk(clk), .clr(clr));  // open: en
  Register #(.width(32)) register_29 (.D(i15), .Q(o15), .clk(clk), .clr(clr));  // open: en
  Register #(.width(32)) register_30 (.D(i23), .Q(o23), .clk(clk), .clr(clr));  // open: en
  Register #(.width(32)) register_31 (.D(i31), .Q(o31), .clk(clk), .clr(clr));  // open: en
  Multiplexer #(.select(5), .width(32), .enable("false")) multiplexer_1 (
    .in0({32{1'b0}}), .in1(o1), .in2(o2), .in3(o3), .in4(o4), .in5(o5), .in6(o6), .in7(o7), .in8(o8),
    .in9(o9), .in10(o10), .in11(o11), .in12(o12), .in13(o13), .in14(o14), .in15(o15), .in16(o16), .in17(o17),
    .in18(o18), .in19(o19), .in20(o20), .in21(o21), .in22(o22), .in23(o23), .in24(o24), .in25(o25),
    .in26(o26), .in27(o27), .in28(o28), .in29(o29), .in30(o30), .in31(o31), .out(RD1), .sel(a1));
  Multiplexer #(.select(5), .width(32), .enable("false")) multiplexer_2 (
    .in0({32{1'b0}}), .in1(o1), .in2(o2), .in3(o3), .in4(o4), .in5(o5), .in6(o6), .in7(o7), .in8(o8),
    .in9(o9), .in10(o10), .in11(o11), .in12(o12), .in13(o13), .in14(o14), .in15(o15), .in16(o16), .in17(o17),
    .in18(o18), .in19(o19), .in20(o20), .in21(o21), .in22(o22), .in23(o23), .in24(o24), .in25(o25),
    .in26(o26), .in27(o27), .in28(o28), .in29(o29), .in30(o30), .in31(o31), .out(RD2), .sel(a2));
endmodule

module ALU (
  input  [31:0] srcA,
  input  [31:0] srcB,
  input  [2:0] ALUControl,
  output [31:0] ALUResult,
  output greater,
  output equal,
  output less
);

  wire [31:0] adduResult, luiReslut, orResult, subuResult;

  Adder #(.width(32)) adder_1 (.a(srcA), .b(srcB), .out(adduResult));  // open: cin, cout
  Subtractor #(.width(32)) subtractor_1 (.a(srcA), .b(srcB), .out(subuResult));  // open: bin, bout
  assign orResult = srcA | srcB;  // OR_Gate or_1, 32 bits wide
  Shifter #(.width(32)) shifter_1 (.in(srcB), .\dist (5'b10000), .out(luiReslut));
  Multiplexer #(.select(3), .width(32), .enable("false")) multiplexer_1 (
    .in0(orResult), .in1(luiReslut), .in2(adduResult), .in6(subuResult), .out(ALUResult), .sel(ALUControl));  // open: in3, in4, in5, in7
  Comparator #(.width(32)) comparator_1 (.a(ALUResult), .b({32{1'b0}}), .gt(greater), .eq(equal), .lt(less));
endmodule

module CONTROLfront (
  input  [5:0] opcode,
  input  [5:0] func,
  output lw,
  output sw,
  output addu,
  output subu,
  output ori,
  output beq,
  output lui,
  output j,
  output jal,
  output jr,
  output sb,
  output lh
);

  wire addu_1_addu, jr_1_jr, special, subu_1_subu;

  jr jr_1 (.func(func), .jr(jr_1_jr));
  addu addu_1 (.func(func), .addu(addu_1_addu));
  lw lw_1 (.opcode(opcode), .lw(lw));
  sw sw_1 (.opcode(opcode), .sw(sw));
  special special_1 (.opcode(opcode), .special(special));
  subu subu_1 (.func(func), .subu(subu_1_subu));
  ori ori_1 (.opcode(opcode), .ori(ori));
  beq beq_1 (.func(opcode), .beq(beq));
  lui lui_1 (.func(opcode), .lui(lui));
  j j_1 (.opcode(opcode), .j(j));
  jal jal_1 (.opcode(opcode), .jal(jal));
  and and_1 (jr, special, jr_1_jr);
  sb sb_1 (.opcode(opcode), .sb(sb));
  lh lh_1 (.opcode(opcode), .lh(lh));
  and and_2 (addu, special, addu_1_addu);
  and and_3 (subu, special, subu_1_subu);
endmodule

module CONTROLback (
  input  lw,
  input  sw,
  input  addu,
  input  subu,
  input  ori,
  input  beq,
  input  lui,
  input  jal,
  input  sb,
  input  lh,
  output RegWrite,
  output MemWrite,
  output [1:0] RegSrc,
  output [1:0] ALUSrc,
  output [1:0] RegAddr3Src,
  output MemSrc,
  output [2:0] ALUOp
);

  wire or_1_out, or_11_out;

  or or_1 (or_1_out, lw, addu, beq, subu, sw);
  or or_2 (RegSrc[0], addu, ori, lh, lui, subu);
  or or_3 (RegSrc[1], jal, lh);
  or or_4 (ALUSrc[0], addu, beq, subu);
  buf or_5 (ALUSrc[1], ori);  // OR_Gate
  buf or_6 (ALUOp[0], lui);  // OR_Gate
  or or_7 (MemWrite, sw, sb);
  Pull_Resistor pull_resistor_1 (.node(MemSrc));
  buf or_8 (MemSrc, sb);  // OR_Gate
  or or_9 (ALUOp[1], or_1_out, sb, lh);
  Pull_Resistor pull_resistor_2 (.node(ALUOp[1]));
  Pull_Resistor pull_resistor_3 (.node(ALUOp[2]));
  or or_10 (ALUOp[2], subu, beq);
  or or_11 (or_11_out, lw, subu, lui, ori, addu, jal);
  Pull_Resistor pull_resistor_4 (.node(MemWrite));
  or or_12 (RegAddr3Src[0], addu, subu);
  buf or_13 (RegAddr3Src[1], jal);  // OR_Gate
  Pull_Resistor pull_resistor_5 (.node(ALUOp[0]));
  or or_14 (RegWrite, or_11_out, lh);
  Pull_Resistor pull_resistor_6 (.node(RegSrc));
  Pull_Resistor pull_resistor_7 (.node(RegWrite));
  Pull_Resistor pull_resistor_8 (.node(ALUSrc));
  Pull_Resistor pull_resistor_9 (.node(RegAddr3Src));
endmodule

module lw (
  input  [5:0] opcode,
  output lw
);

  wire not_1_out, not_2_out, not_3_out;

  not not_1 (not_1_out, opcode[2]);
  not not_2 (not_2_out, opcode[3]);
  not not_3 (not_3_out, opcode[4]);
  and and_1 (lw, opcode[0], opcode[1], not_1_out, not_2_out, not_3_out, opcode[5]);
endmodule

module sw (
  input  [5:0] opcode,
  output sw
);

  wire not_1_out, not_2_out;

  not not_1 (not_1_out, opcode[2]);
  not not_2 (not_2_out, opcode[4]);
  and and_1 (sw, opcode[0], opcode[1], not_1_out, opcode[3], not_2_out, opcode[5]);
endmodule

module special (
  input  [5:0] opcode,
  output special
);

  wire not_1_out, not_2_out, not_3_out, not_4_out, not_5_out, not_6_out;

  not not_1 (not_1_out, opcode[0]);
  not not_2 (not_2_out, opcode[1]);
  not not_3 (not_3_out, opcode[2]);
  not not_4 (not_4_out, opcode[3]);
  not not_5 (not_5_out, opcode[4]);
  not not_6 (not_6_out, opcode[5]);
  and and_1 (special, not_1_out, not_2_out, not_3_out, not_4_out, not_5_out, not_6_out);
endmodule

module addu (
  input  [5:0] func,
  output addu
);

  wire not_1_out, not_2_out, not_3_out, not_4_out;

  not not_1 (not_1_out, func[1]);
  not not_2 (not_2_out, func[2]);
  not not_3 (not_3_out, func[3]);
  not not_4 (not_4_out, func[4]);
  and and_1 (addu, func[0], not_1_out, not_2_out, not_3_out, not_4_out, func[5]);
endmodule

module subu (
  input  [5:0] func,
  output subu
);

  wire not_1_out, not_2_out, not_3_out;

  not not_1 (not_1_out, func[2]);
  not not_2 (not_2_out, func[3]);
  not not_3 (not_3_out, func[4]);
  and and_1 (subu, func[0], func[1], not_1_out, not_2_out, not_3_out, func[5]);
endmodule

module ori (
  input  [5:0] opcode,
  output ori
);

  wire not_1_out, not_2_out, not_3_out;

  not not_1 (not_1_out, opcode[1]);
  not not_2 (not_2_out, opcode[4]);
  not not_3 (not_3_out, opcode[5]);
  and and_1 (ori, opcode[0], not_1_out, opcode[2], opcode[3], not_2_out, not_3_out);
endmodule

module beq (
  input  [5:0] func,
  output beq
);

  wire not_1_out, not_2_out, not_3_out, not_4_out, not_5_out;

  not not_1 (not_1_out, func[0]);
  not not_2 (not_2_out, func[1]);
  not not_3 (not_3_out, func[3]);
  not not_4 (not_4_out, func[4]);
  not not_5 (not_5_out, func[5]);
  and and_1 (beq, not_1_out, not_2_out, func[2], not_3_out, not_4_out, not_5_out);
endmodule

module lui (
  input  [5:0] func,
  output lui
);

  wire not_1_out, not_2_out;

  not not_1 (not_1_out, func[4]);
  not not_2 (not_2_out, func[5]);
  and and_1 (lui, func[0], func[1], func[2], func[3], not_1_out, not_2_out);
endmodule

module top (
);

  main main_1 ();  // open: clr, instr, RegWrite, RegAddr, MemWrite, MemAddr, MemData, RegData
endmodule

module j (
  input  [5:0] opcode,
  output j
);

  wire not_1_out, not_2_out, not_3_out, not_4_out, not_5_out;

  not not_1 (not_1_out, opcode[0]);
  not not_2 (not_2_out, opcode[2]);
  not not_3 (not_3_out, opcode[3]);
  not not_4 (not_4_out, opcode[4]);
  not not_5 (not_5_out, opcode[5]);
  and and_1 (j, not_1_out, opcode[1], not_2_out, not_3_out, not_4_out, not_5_out);
endmodule

module jal (
  input  [5:0] opcode,
  output jal
);

  wire not_1_out, not_2_out, not_3_out, not_4_out;

  not not_1 (not_1_out, opcode[2]);
  not not_2 (not_2_out, opcode[3]);
  not not_3 (not_3_out, opcode[4]);
  not not_4 (not_4_out, opcode[5]);
  and and_1 (jal, opcode[0], opcode[1], not_1_out, not_2_out, not_3_out, not_4_out);
endmodule

module jr (
  input  [5:0] func,
  output jr
);

  wire not_1_out, not_2_out, not_3_out, not_4_out, not_5_out;

  not not_1 (not_1_out, func[0]);
  not not_2 (not_2_out, func[1]);
  not not_3 (not_3_out, func[2]);
  not not_4 (not_4_out, func[4]);
  not not_5 (not_5_out, func[5]);
  and and_1 (jr, not_1_out, not_2_out, not_3_out, func[3], not_4_out, not_5_out);
endmodule

module sb (
  input  [5:0] opcode,
  output sb
);

  wire not_1_out, not_2_out, not_3_out, not_4_out;

  not not_1 (not_1_out, opcode[0]);
  not not_2 (not_2_out, opcode[1]);
  not not_3 (not_3_out, opcode[2]);
  not not_4 (not_4_out, opcode[4]);
  and and_1 (sb, not_1_out, not_2_out, not_3_out, opcode[3], not_4_out, opcode[5]);
endmodule

module smask (
  input  [31:0] R2,
  input  [31:0] MemAdd,
  output [31:0] ans
);

  wire [4:0] bit_extender_1_out, shifter_1_out;

  assign bit_extender_1_out = {{3{1'b0}}, MemAdd[1:0]};  // Bit_Extender bit_extender_1
  Shifter #(.width(5)) shifter_1 (.in(bit_extender_1_out), .\dist (3'b011), .out(shifter_1_out));
  // Probe on shifter_1_out
  Shifter #(.width(32)) shifter_2 (.in(R2), .\dist (shifter_1_out), .out(ans));
  // Probe on ans

  // Other names for the same wires on the sheet: select[1:0] = MemAdd[1:0]
endmodule

module lh (
  input  [5:0] opcode,
  output lh
);

  wire not_1_out, not_2_out, not_3_out, not_4_out;

  not not_1 (not_1_out, opcode[1]);
  not not_2 (not_2_out, opcode[2]);
  not not_3 (not_3_out, opcode[3]);
  not not_4 (not_4_out, opcode[4]);
  and and_1 (lh, opcode[0], not_1_out, not_2_out, not_3_out, not_4_out, opcode[5]);
endmodule

module lmask (
  input  [31:0] MemDataOut,
  input  [31:0] MemAdd,
  output [31:0] ans
);

  Multiplexer #(.width(16), .enable("false")) multiplexer_1 (
    .in0(MemDataOut[15:0]), .in1(MemDataOut[31:16]), .out(ans[15:0]), .sel(MemAdd[1]));

  assign ans[31:16] = {16{1'b0}};

  // Other names for the same wires on the sheet: sel = MemAdd[1]
endmodule
