// Logisim project 4bit_sort.circ as structural Verilog
module _1bit_swap (
  input  I1,
  input  I2,
  input  S,
  output O1,
  output O2
);

  wire and_1_out, and_2_out, and_3_out, and_4_out, not_1_out;

  not not_1 (not_1_out, S);
  and and_1 (and_1_out, I1, not_1_out);
  and and_2 (and_2_out, I2, S);
  and and_3 (and_3_out, I2, not_1_out);
  and and_4 (and_4_out, I1, S);
  or or_1 (O1, and_1_out, and_2_out);
  or or_2 (O2, and_3_out, and_4_out);
endmodule

module _4bit_swap (
  input  [3:0] in_1,
  input  [3:0] in_2,
  input  in_3,
  output [3:0] out_4,
  output [3:0] out_5
);

  _1bit_swap u_1bit_swap_1 (.I1(in_1[0]), .I2(in_2[0]), .S(in_3), .O1(out_4[0]), .O2(out_5[0]));
  _1bit_swap u_1bit_swap_2 (.I1(in_1[1]), .I2(in_2[1]), .S(in_3), .O1(out_4[1]), .O2(out_5[1]));
  _1bit_swap u_1bit_swap_3 (.I1(in_1[2]), .I2(in_2[2]), .S(in_3), .O1(out_4[2]), .O2(out_5[2]));
  _1bit_swap u_1bit_swap_4 (.I1(in_1[3]), .I2(in_2[3]), .S(in_3), .O1(out_4[3]), .O2(out_5[3]));
endmodule

module _4bit_sort (
  input  [3:0] in_1,
  input  [3:0] in_2,
  input  [3:0] in_3,
  input  [3:0] in_4,
  output [3:0] out_5,
  output [3:0] out_6,
  output [3:0] out_7,
  output [3:0] out_8
);

  wire [3:0] n4bit_comp_change_1_out_3, n4bit_comp_change_1_out_4, n4bit_comp_change_2_out_3,
       n4bit_comp_change_2_out_4, n4bit_comp_change_3_out_4, n4bit_comp_change_4_out_3;

  _4bit_comp_change u_4bit_comp_change_1 (
    .A(in_1), .B(in_2), .out_3(n4bit_comp_change_1_out_3), .out_4(n4bit_comp_change_1_out_4));
  _4bit_comp_change u_4bit_comp_change_2 (
    .A(in_3), .B(in_4), .out_3(n4bit_comp_change_2_out_3), .out_4(n4bit_comp_change_2_out_4));
  _4bit_comp_change u_4bit_comp_change_3 (
    .A(n4bit_comp_change_1_out_3), .B(n4bit_comp_change_2_out_3), .out_3(out_5),
    .out_4(n4bit_comp_change_3_out_4));
  _4bit_comp_change u_4bit_comp_change_4 (
    .A(n4bit_comp_change_1_out_4), .B(n4bit_comp_change_2_out_4), .out_3(n4bit_comp_change_4_out_3),
    .out_4(out_8));
  _4bit_comp_change u_4bit_comp_change_5 (
    .A(n4bit_comp_change_3_out_4), .B(n4bit_comp_change_4_out_3), .out_3(out_6), .out_4(out_7));
endmodule

module _4bit_comp_change (
  input  [3:0] A,
  input  [3:0] B,
  output [3:0] out_3,
  output [3:0] out_4
);

  wire comparator_1_gt;

  Comparator #(.width(4), .mode("unsigned")) comparator_1 (.a(A), .b(B), .gt(comparator_1_gt));  // open: eq, lt
  _4bit_swap u_4bit_swap_1 (.in_1(A), .in_2(B), .in_3(comparator_1_gt), .out_4(out_3), .out_5(out_4));
endmodule
