// Logisim project swap.circ as structural Verilog: 2 circuits, main circuit main
module main (
  input  I1,
  input  I2,
  input  S,
  output O1,
  output O2
);

  wire not_1_out;

  not not_1 (not_1_out, S);
  assign O1 = not_1_out ? I1 : 1'bz;  // Controlled_Buffer controlled_buffer_1
  assign O1 = S ? I2 : 1'bz;  // Controlled_Buffer controlled_buffer_2
  assign O2 = not_1_out ? I2 : 1'bz;  // Controlled_Buffer controlled_buffer_3
  assign O2 = S ? I1 : 1'bz;  // Controlled_Buffer controlled_buffer_4
endmodule

module swap (
  input  I1,
  input  I2,
  input  S,
  output O1,
  output O2
);

  wire not_1_out;

  not not_1 (not_1_out, S);
  assign O1 = not_1_out ? I1 : 1'bz;  // Controlled_Buffer controlled_buffer_1
  assign O1 = S ? I2 : 1'bz;  // Controlled_Buffer controlled_buffer_2
  assign O2 = not_1_out ? I2 : 1'bz;  // Controlled_Buffer controlled_buffer_3
  assign O2 = S ? I1 : 1'bz;  // Controlled_Buffer controlled_buffer_4
endmodule
